# Fritzing sketch RadioArduino (saved by Fritzing 0.9.3b)
breadboards: 2

parts:
  TEA5767 = IC, SIP package, 4 pins [chip_label=5767]
  R1 = Rotary Potentiometer (Small) [maximum_resistance=10kΩ package=THT]
  R2 = Rotary Potentiometer (Small) [maximum_resistance=10kΩ package=THT]
  LCD = LCD-16X2 [package=lcd-16x2]
  NodeMCU = NodeMCU V3.0

nets:
  VDD: TEA5767.pin1, R1.leg2, R2.leg2, LCD.VDD, LCD.A, NodeMCU.3V3
  N1: TEA5767.pin2, NodeMCU.D2
  N2: TEA5767.pin3, NodeMCU.D1
  N3: TEA5767.pin4, R1.leg1, R2.leg1, LCD.VSS, LCD.R_W, LCD.K, NodeMCU.GND#6, NodeMCU.GND#13, NodeMCU.GND#16, NodeMCU.GND#33
  N4: R1.wiper, NodeMCU.A0
  N5: R2.wiper, LCD.VO
  N6: LCD.RS, NodeMCU.D3
  N7: LCD.E, NodeMCU.D4
  N8: LCD.DB4, NodeMCU.D5
  N9: LCD.DB5, NodeMCU.D6
  N10: LCD.DB6, NodeMCU.D7
  N11: LCD.DB7, NodeMCU.D8

custom parts:
  NodeMCU V3.0: ESP8266 based NodeMCU
